// Logisim project screen.circ as structural Verilog: 3 circuits, main circuit main
module main (
);

  wire clock_1_out, comparator_1_eq, demultiplexer_1_out0, demultiplexer_1_out1, demultiplexer_1_out2,
       demultiplexer_1_out3, demultiplexer_1_out4, demultiplexer_1_out5, demultiplexer_1_out6,
       demultiplexer_1_out7, demultiplexer_1_out8, demultiplexer_1_out9, demultiplexer_1_out10,
       demultiplexer_1_out11, demultiplexer_1_out12, demultiplexer_1_out13, demultiplexer_1_out14,
       demultiplexer_1_out15, demultiplexer_1_out16, demultiplexer_1_out17, demultiplexer_1_out18,
       demultiplexer_1_out19, demultiplexer_1_out20, demultiplexer_1_out21, demultiplexer_1_out22,
       demultiplexer_1_out23, demultiplexer_1_out24, demultiplexer_1_out25, demultiplexer_1_out26,
       demultiplexer_1_out27, demultiplexer_1_out28, demultiplexer_1_out29, demultiplexer_1_out30,
       demultiplexer_1_out31, demultiplexer_2_out0, demultiplexer_2_out1, demultiplexer_2_out2,
       demultiplexer_2_out3, demultiplexer_2_out4, demultiplexer_2_out5, demultiplexer_2_out6,
       demultiplexer_2_out7, demultiplexer_2_out8, demultiplexer_2_out9, demultiplexer_2_out10,
       demultiplexer_2_out11, demultiplexer_2_out12, demultiplexer_2_out13, demultiplexer_2_out14,
       demultiplexer_2_out15, demultiplexer_2_out16, demultiplexer_2_out17, demultiplexer_2_out18,
       demultiplexer_2_out19, demultiplexer_2_out20, demultiplexer_2_out21, demultiplexer_2_out22,
       demultiplexer_2_out23, demultiplexer_2_out24, demultiplexer_2_out25, demultiplexer_2_out26,
       demultiplexer_2_out27, demultiplexer_2_out28, demultiplexer_2_out29, demultiplexer_2_out30,
       demultiplexer_2_out31, demultiplexer_3_out0, demultiplexer_3_out1, demultiplexer_3_out2,
       demultiplexer_3_out3, demultiplexer_3_out4, demultiplexer_3_out5, demultiplexer_3_out6,
       demultiplexer_3_out7, demultiplexer_3_out8, demultiplexer_3_out9, demultiplexer_3_out10,
       demultiplexer_3_out11, demultiplexer_3_out12, demultiplexer_3_out13, demultiplexer_3_out14,
       demultiplexer_3_out15, demultiplexer_3_out16, demultiplexer_3_out17, demultiplexer_3_out18,
       demultiplexer_3_out19, demultiplexer_3_out20, demultiplexer_3_out21, demultiplexer_3_out22,
       demultiplexer_3_out23, demultiplexer_3_out24, demultiplexer_3_out25, demultiplexer_3_out26,
       demultiplexer_3_out27, demultiplexer_3_out28, demultiplexer_3_out29, demultiplexer_3_out30,
       demultiplexer_3_out31, demultiplexer_4_out0, demultiplexer_4_out1, demultiplexer_4_out2,
       demultiplexer_4_out3, demultiplexer_4_out4, demultiplexer_4_out5, demultiplexer_4_out6,
       demultiplexer_4_out7, demultiplexer_4_out8, demultiplexer_4_out9, demultiplexer_4_out10,
       demultiplexer_4_out11, demultiplexer_4_out12, demultiplexer_4_out13, demultiplexer_4_out14,
       demultiplexer_4_out15, demultiplexer_4_out16, demultiplexer_4_out17, demultiplexer_4_out18,
       demultiplexer_4_out19, demultiplexer_4_out20, demultiplexer_4_out21, demultiplexer_4_out22,
       demultiplexer_4_out23, demultiplexer_4_out24, demultiplexer_4_out25, demultiplexer_4_out26,
       demultiplexer_4_out27, demultiplexer_4_out28, demultiplexer_4_out29, demultiplexer_4_out30,
       demultiplexer_4_out31, not_1_out;
  wire [4:0] Row_q;
  wire [19:0] Address_q;
  wire [31:0] counter_1_q, pixelmem2_1_pixelout, pixelmem2_2_pixelout, pixelmem2_3_pixelout,
       pixelmem2_4_pixelout, pixelmem2_5_pixelout, pixelmem2_6_pixelout, pixelmem2_7_pixelout,
       pixelmem2_8_pixelout, pixelmem2_9_pixelout, pixelmem2_10_pixelout, pixelmem2_11_pixelout,
       pixelmem2_12_pixelout, pixelmem2_13_pixelout, pixelmem2_14_pixelout, pixelmem2_15_pixelout,
       pixelmem2_16_pixelout, pixelmem2_17_pixelout, pixelmem2_18_pixelout, pixelmem2_19_pixelout,
       pixelmem2_20_pixelout, pixelmem2_21_pixelout, pixelmem2_22_pixelout, pixelmem2_23_pixelout,
       pixelmem2_24_pixelout, pixelmem2_25_pixelout, pixelmem2_26_pixelout, pixelmem2_27_pixelout,
       pixelmem2_28_pixelout, pixelmem2_29_pixelout, pixelmem2_30_pixelout, pixelmem2_31_pixelout,
       pixelmem2_32_pixelout, pixelmem2_33_pixelout, pixelmem2_34_pixelout, pixelmem2_35_pixelout,
       pixelmem2_36_pixelout, pixelmem2_37_pixelout, pixelmem2_38_pixelout, pixelmem2_39_pixelout,
       pixelmem2_40_pixelout, pixelmem2_41_pixelout, pixelmem2_42_pixelout, pixelmem2_43_pixelout,
       pixelmem2_44_pixelout, pixelmem2_45_pixelout, pixelmem2_46_pixelout, pixelmem2_47_pixelout,
       pixelmem2_48_pixelout, pixelmem2_49_pixelout, pixelmem2_50_pixelout, pixelmem2_51_pixelout,
       pixelmem2_52_pixelout, pixelmem2_53_pixelout, pixelmem2_54_pixelout, pixelmem2_55_pixelout,
       pixelmem2_56_pixelout, pixelmem2_57_pixelout, pixelmem2_58_pixelout, pixelmem2_59_pixelout,
       pixelmem2_60_pixelout, pixelmem2_61_pixelout, pixelmem2_62_pixelout, pixelmem2_63_pixelout,
       pixelmem2_64_pixelout, pixelmem_1_pixelout, pixelmem_2_pixelout, pixelmem_3_pixelout,
       pixelmem_4_pixelout, pixelmem_5_pixelout, pixelmem_6_pixelout, pixelmem_7_pixelout,
       pixelmem_8_pixelout, pixelmem_9_pixelout, pixelmem_10_pixelout, pixelmem_11_pixelout,
       pixelmem_12_pixelout, pixelmem_13_pixelout, pixelmem_14_pixelout, pixelmem_15_pixelout,
       pixelmem_16_pixelout, pixelmem_17_pixelout, pixelmem_18_pixelout, pixelmem_19_pixelout,
       pixelmem_20_pixelout, pixelmem_21_pixelout, pixelmem_22_pixelout, pixelmem_23_pixelout,
       pixelmem_24_pixelout, pixelmem_25_pixelout, pixelmem_26_pixelout, pixelmem_27_pixelout,
       pixelmem_28_pixelout, pixelmem_29_pixelout, pixelmem_30_pixelout, pixelmem_31_pixelout,
       pixelmem_32_pixelout, pixelmem_33_pixelout, pixelmem_34_pixelout, pixelmem_35_pixelout,
       pixelmem_36_pixelout, pixelmem_37_pixelout, pixelmem_38_pixelout, pixelmem_39_pixelout,
       pixelmem_40_pixelout, pixelmem_41_pixelout, pixelmem_42_pixelout, pixelmem_43_pixelout,
       pixelmem_44_pixelout, pixelmem_45_pixelout, pixelmem_46_pixelout, pixelmem_47_pixelout,
       pixelmem_48_pixelout, pixelmem_49_pixelout, pixelmem_50_pixelout, pixelmem_51_pixelout,
       pixelmem_52_pixelout, pixelmem_53_pixelout, pixelmem_54_pixelout, pixelmem_55_pixelout,
       pixelmem_56_pixelout, pixelmem_57_pixelout, pixelmem_58_pixelout, pixelmem_59_pixelout,
       pixelmem_60_pixelout, pixelmem_61_pixelout, pixelmem_62_pixelout, pixelmem_63_pixelout,
       pixelmem_64_pixelout, rom_1_data, rom_2_data, rom_3_data, rom_4_data;

  ROM #(.addrWidth(20), .dataWidth(32)) rom_1 (.addr(Address_q), .data(rom_1_data));  // open: sel
  ROM #(.addrWidth(20), .dataWidth(32)) rom_2 (.addr(Address_q), .data(rom_2_data));  // open: sel
  Demultiplexer #(.select(5)) demultiplexer_1 (
    .out0(demultiplexer_1_out0), .out1(demultiplexer_1_out1), .out2(demultiplexer_1_out2),
    .out3(demultiplexer_1_out3), .out4(demultiplexer_1_out4), .out5(demultiplexer_1_out5),
    .out6(demultiplexer_1_out6), .out7(demultiplexer_1_out7), .out8(demultiplexer_1_out8),
    .out9(demultiplexer_1_out9), .out10(demultiplexer_1_out10), .out11(demultiplexer_1_out11),
    .out12(demultiplexer_1_out12), .out13(demultiplexer_1_out13), .out14(demultiplexer_1_out14),
    .out15(demultiplexer_1_out15), .out16(demultiplexer_1_out16), .out17(demultiplexer_1_out17),
    .out18(demultiplexer_1_out18), .out19(demultiplexer_1_out19), .out20(demultiplexer_1_out20),
    .out21(demultiplexer_1_out21), .out22(demultiplexer_1_out22), .out23(demultiplexer_1_out23),
    .out24(demultiplexer_1_out24), .out25(demultiplexer_1_out25), .out26(demultiplexer_1_out26),
    .out27(demultiplexer_1_out27), .out28(demultiplexer_1_out28), .out29(demultiplexer_1_out29),
    .out30(demultiplexer_1_out30), .out31(demultiplexer_1_out31), .in(not_1_out), .sel(Row_q));  // open: en
  Demultiplexer #(.select(5)) demultiplexer_2 (
    .out0(demultiplexer_2_out0), .out1(demultiplexer_2_out1), .out2(demultiplexer_2_out2),
    .out3(demultiplexer_2_out3), .out4(demultiplexer_2_out4), .out5(demultiplexer_2_out5),
    .out6(demultiplexer_2_out6), .out7(demultiplexer_2_out7), .out8(demultiplexer_2_out8),
    .out9(demultiplexer_2_out9), .out10(demultiplexer_2_out10), .out11(demultiplexer_2_out11),
    .out12(demultiplexer_2_out12), .out13(demultiplexer_2_out13), .out14(demultiplexer_2_out14),
    .out15(demultiplexer_2_out15), .out16(demultiplexer_2_out16), .out17(demultiplexer_2_out17),
    .out18(demultiplexer_2_out18), .out19(demultiplexer_2_out19), .out20(demultiplexer_2_out20),
    .out21(demultiplexer_2_out21), .out22(demultiplexer_2_out22), .out23(demultiplexer_2_out23),
    .out24(demultiplexer_2_out24), .out25(demultiplexer_2_out25), .out26(demultiplexer_2_out26),
    .out27(demultiplexer_2_out27), .out28(demultiplexer_2_out28), .out29(demultiplexer_2_out29),
    .out30(demultiplexer_2_out30), .out31(demultiplexer_2_out31), .in(not_1_out), .sel(Row_q));  // open: en
  Clock clock_1 (.out(clock_1_out));
  pixelmem pixelmem_1 (
    .Data(rom_1_data), .Store(demultiplexer_1_out0), .PixelOut(pixelmem_1_pixelout), .Draw(comparator_1_eq));
  pixelmem pixelmem_2 (
    .Data(rom_1_data), .Store(demultiplexer_1_out1), .PixelOut(pixelmem_2_pixelout), .Draw(comparator_1_eq));
  DotMatrix #(.inputtype("row"), .matrixcols(32), .matrixrows(32), .persist(1)) dotmatrix_1 (
    .row0(pixelmem_1_pixelout), .row1(pixelmem_2_pixelout), .row2(pixelmem_3_pixelout),
    .row3(pixelmem_4_pixelout), .row4(pixelmem_5_pixelout), .row5(pixelmem_6_pixelout),
    .row6(pixelmem_7_pixelout), .row7(pixelmem_8_pixelout), .row8(pixelmem_9_pixelout),
    .row9(pixelmem_10_pixelout), .row10(pixelmem_11_pixelout), .row11(pixelmem_12_pixelout),
    .row12(pixelmem_13_pixelout), .row13(pixelmem_14_pixelout), .row14(pixelmem_15_pixelout),
    .row15(pixelmem_16_pixelout), .row16(pixelmem_17_pixelout), .row17(pixelmem_18_pixelout),
    .row18(pixelmem_19_pixelout), .row19(pixelmem_20_pixelout), .row20(pixelmem_21_pixelout),
    .row21(pixelmem_22_pixelout), .row22(pixelmem_23_pixelout), .row23(pixelmem_24_pixelout),
    .row24(pixelmem_25_pixelout), .row25(pixelmem_26_pixelout), .row26(pixelmem_27_pixelout),
    .row27(pixelmem_28_pixelout), .row28(pixelmem_29_pixelout), .row29(pixelmem_30_pixelout),
    .row30(pixelmem_31_pixelout), .row31(pixelmem_32_pixelout));
  pixelmem pixelmem_3 (
    .Data(rom_1_data), .Store(demultiplexer_1_out2), .PixelOut(pixelmem_3_pixelout), .Draw(comparator_1_eq));
  pixelmem pixelmem_4 (
    .Data(rom_1_data), .Store(demultiplexer_1_out3), .PixelOut(pixelmem_4_pixelout), .Draw(comparator_1_eq));
  pixelmem pixelmem_5 (
    .Data(rom_1_data), .Store(demultiplexer_1_out4), .PixelOut(pixelmem_5_pixelout), .Draw(comparator_1_eq));
  pixelmem pixelmem_6 (
    .Data(rom_1_data), .Store(demultiplexer_1_out5), .PixelOut(pixelmem_6_pixelout), .Draw(comparator_1_eq));
  pixelmem pixelmem_7 (
    .Data(rom_1_data), .Store(demultiplexer_1_out6), .PixelOut(pixelmem_7_pixelout), .Draw(comparator_1_eq));
  pixelmem pixelmem_8 (
    .Data(rom_1_data), .Store(demultiplexer_1_out7), .PixelOut(pixelmem_8_pixelout), .Draw(comparator_1_eq));
  pixelmem pixelmem_9 (
    .Data(rom_1_data), .Store(demultiplexer_1_out8), .PixelOut(pixelmem_9_pixelout), .Draw(comparator_1_eq));
  pixelmem pixelmem_10 (
    .Data(rom_1_data), .Store(demultiplexer_1_out9), .PixelOut(pixelmem_10_pixelout), .Draw(comparator_1_eq));
  pixelmem pixelmem_11 (
    .Data(rom_1_data), .Store(demultiplexer_1_out10), .PixelOut(pixelmem_11_pixelout), .Draw(comparator_1_eq));
  pixelmem pixelmem_12 (
    .Data(rom_1_data), .Store(demultiplexer_1_out11), .PixelOut(pixelmem_12_pixelout), .Draw(comparator_1_eq));
  pixelmem pixelmem_13 (
    .Data(rom_1_data), .Store(demultiplexer_1_out12), .PixelOut(pixelmem_13_pixelout), .Draw(comparator_1_eq));
  pixelmem pixelmem_14 (
    .Data(rom_1_data), .Store(demultiplexer_1_out13), .PixelOut(pixelmem_14_pixelout), .Draw(comparator_1_eq));
  pixelmem pixelmem_15 (
    .Data(rom_1_data), .Store(demultiplexer_1_out14), .PixelOut(pixelmem_15_pixelout), .Draw(comparator_1_eq));
  pixelmem pixelmem_16 (
    .Data(rom_1_data), .Store(demultiplexer_1_out15), .PixelOut(pixelmem_16_pixelout), .Draw(comparator_1_eq));
  pixelmem pixelmem_17 (
    .Data(rom_1_data), .Store(demultiplexer_1_out16), .PixelOut(pixelmem_17_pixelout), .Draw(comparator_1_eq));
  pixelmem pixelmem_18 (
    .Data(rom_1_data), .Store(demultiplexer_1_out17), .PixelOut(pixelmem_18_pixelout), .Draw(comparator_1_eq));
  pixelmem pixelmem_19 (
    .Data(rom_1_data), .Store(demultiplexer_1_out18), .PixelOut(pixelmem_19_pixelout), .Draw(comparator_1_eq));
  pixelmem pixelmem_20 (
    .Data(rom_1_data), .Store(demultiplexer_1_out19), .PixelOut(pixelmem_20_pixelout), .Draw(comparator_1_eq));
  pixelmem pixelmem_21 (
    .Data(rom_1_data), .Store(demultiplexer_1_out20), .PixelOut(pixelmem_21_pixelout), .Draw(comparator_1_eq));
  pixelmem pixelmem_22 (
    .Data(rom_1_data), .Store(demultiplexer_1_out21), .PixelOut(pixelmem_22_pixelout), .Draw(comparator_1_eq));
  pixelmem pixelmem_23 (
    .Data(rom_1_data), .Store(demultiplexer_1_out22), .PixelOut(pixelmem_23_pixelout), .Draw(comparator_1_eq));
  pixelmem pixelmem_24 (
    .Data(rom_1_data), .Store(demultiplexer_1_out23), .PixelOut(pixelmem_24_pixelout), .Draw(comparator_1_eq));
  pixelmem pixelmem_25 (
    .Data(rom_1_data), .Store(demultiplexer_1_out24), .PixelOut(pixelmem_25_pixelout), .Draw(comparator_1_eq));
  pixelmem pixelmem_26 (
    .Data(rom_1_data), .Store(demultiplexer_1_out25), .PixelOut(pixelmem_26_pixelout), .Draw(comparator_1_eq));
  pixelmem pixelmem_27 (
    .Data(rom_1_data), .Store(demultiplexer_1_out26), .PixelOut(pixelmem_27_pixelout), .Draw(comparator_1_eq));
  pixelmem pixelmem_28 (
    .Data(rom_1_data), .Store(demultiplexer_1_out27), .PixelOut(pixelmem_28_pixelout), .Draw(comparator_1_eq));
  pixelmem pixelmem_29 (
    .Data(rom_1_data), .Store(demultiplexer_1_out28), .PixelOut(pixelmem_29_pixelout), .Draw(comparator_1_eq));
  pixelmem pixelmem_30 (
    .Data(rom_1_data), .Store(demultiplexer_1_out29), .PixelOut(pixelmem_30_pixelout), .Draw(comparator_1_eq));
  pixelmem pixelmem_31 (
    .Data(rom_1_data), .Store(demultiplexer_1_out30), .PixelOut(pixelmem_31_pixelout), .Draw(comparator_1_eq));
  pixelmem pixelmem_32 (
    .Data(rom_1_data), .Store(demultiplexer_1_out31), .PixelOut(pixelmem_32_pixelout), .Draw(comparator_1_eq));
  pixelmem2 pixelmem2_1 (
    .Data(rom_2_data), .PixelOut(pixelmem2_1_pixelout), .Store(demultiplexer_2_out0), .Draw(comparator_1_eq));
  DotMatrix #(.inputtype("row"), .matrixcols(32), .matrixrows(32), .persist(1)) dotmatrix_2 (
    .row0(pixelmem2_1_pixelout), .row1(pixelmem2_2_pixelout), .row2(pixelmem2_3_pixelout),
    .row3(pixelmem2_4_pixelout), .row4(pixelmem2_5_pixelout), .row5(pixelmem2_6_pixelout),
    .row6(pixelmem2_7_pixelout), .row7(pixelmem2_8_pixelout), .row8(pixelmem2_9_pixelout),
    .row9(pixelmem2_10_pixelout), .row10(pixelmem2_11_pixelout), .row11(pixelmem2_12_pixelout),
    .row12(pixelmem2_13_pixelout), .row13(pixelmem2_14_pixelout), .row14(pixelmem2_15_pixelout),
    .row15(pixelmem2_16_pixelout), .row16(pixelmem2_17_pixelout), .row17(pixelmem2_18_pixelout),
    .row18(pixelmem2_19_pixelout), .row19(pixelmem2_20_pixelout), .row20(pixelmem2_21_pixelout),
    .row21(pixelmem2_22_pixelout), .row22(pixelmem2_23_pixelout), .row23(pixelmem2_24_pixelout),
    .row24(pixelmem2_25_pixelout), .row25(pixelmem2_26_pixelout), .row26(pixelmem2_27_pixelout),
    .row27(pixelmem2_28_pixelout), .row28(pixelmem2_29_pixelout), .row29(pixelmem2_30_pixelout),
    .row30(pixelmem2_31_pixelout), .row31(pixelmem2_32_pixelout));
  pixelmem2 pixelmem2_2 (
    .Data(rom_2_data), .PixelOut(pixelmem2_2_pixelout), .Store(demultiplexer_2_out1), .Draw(comparator_1_eq));
  pixelmem2 pixelmem2_3 (
    .Data(rom_2_data), .PixelOut(pixelmem2_3_pixelout), .Store(demultiplexer_2_out2), .Draw(comparator_1_eq));
  pixelmem2 pixelmem2_4 (
    .Data(rom_2_data), .PixelOut(pixelmem2_4_pixelout), .Store(demultiplexer_2_out3), .Draw(comparator_1_eq));
  pixelmem2 pixelmem2_5 (
    .Data(rom_2_data), .PixelOut(pixelmem2_5_pixelout), .Store(demultiplexer_2_out4), .Draw(comparator_1_eq));
  pixelmem2 pixelmem2_6 (
    .Data(rom_2_data), .PixelOut(pixelmem2_6_pixelout), .Store(demultiplexer_2_out5), .Draw(comparator_1_eq));
  pixelmem2 pixelmem2_7 (
    .Data(rom_2_data), .PixelOut(pixelmem2_7_pixelout), .Store(demultiplexer_2_out6), .Draw(comparator_1_eq));
  pixelmem2 pixelmem2_8 (
    .Data(rom_2_data), .PixelOut(pixelmem2_8_pixelout), .Store(demultiplexer_2_out7), .Draw(comparator_1_eq));
  pixelmem2 pixelmem2_9 (
    .Data(rom_2_data), .PixelOut(pixelmem2_9_pixelout), .Store(demultiplexer_2_out8), .Draw(comparator_1_eq));
  pixelmem2 pixelmem2_10 (
    .Data(rom_2_data), .PixelOut(pixelmem2_10_pixelout), .Store(demultiplexer_2_out9), .Draw(comparator_1_eq));
  pixelmem2 pixelmem2_11 (
    .Data(rom_2_data), .PixelOut(pixelmem2_11_pixelout), .Store(demultiplexer_2_out10), .Draw(comparator_1_eq));
  pixelmem2 pixelmem2_12 (
    .Data(rom_2_data), .PixelOut(pixelmem2_12_pixelout), .Store(demultiplexer_2_out11), .Draw(comparator_1_eq));
  pixelmem2 pixelmem2_13 (
    .Data(rom_2_data), .PixelOut(pixelmem2_13_pixelout), .Store(demultiplexer_2_out12), .Draw(comparator_1_eq));
  pixelmem2 pixelmem2_14 (
    .Data(rom_2_data), .PixelOut(pixelmem2_14_pixelout), .Store(demultiplexer_2_out13), .Draw(comparator_1_eq));
  pixelmem2 pixelmem2_15 (
    .Data(rom_2_data), .PixelOut(pixelmem2_15_pixelout), .Store(demultiplexer_2_out14), .Draw(comparator_1_eq));
  pixelmem2 pixelmem2_16 (
    .Data(rom_2_data), .PixelOut(pixelmem2_16_pixelout), .Store(demultiplexer_2_out15), .Draw(comparator_1_eq));
  pixelmem2 pixelmem2_17 (
    .Data(rom_2_data), .PixelOut(pixelmem2_17_pixelout), .Store(demultiplexer_2_out16), .Draw(comparator_1_eq));
  pixelmem2 pixelmem2_18 (
    .Data(rom_2_data), .PixelOut(pixelmem2_18_pixelout), .Store(demultiplexer_2_out17), .Draw(comparator_1_eq));
  pixelmem2 pixelmem2_19 (
    .Data(rom_2_data), .PixelOut(pixelmem2_19_pixelout), .Store(demultiplexer_2_out18), .Draw(comparator_1_eq));
  pixelmem2 pixelmem2_20 (
    .Data(rom_2_data), .PixelOut(pixelmem2_20_pixelout), .Store(demultiplexer_2_out19), .Draw(comparator_1_eq));
  pixelmem2 pixelmem2_21 (
    .Data(rom_2_data), .PixelOut(pixelmem2_21_pixelout), .Store(demultiplexer_2_out20), .Draw(comparator_1_eq));
  pixelmem2 pixelmem2_22 (
    .Data(rom_2_data), .PixelOut(pixelmem2_22_pixelout), .Store(demultiplexer_2_out21), .Draw(comparator_1_eq));
  pixelmem2 pixelmem2_23 (
    .Data(rom_2_data), .PixelOut(pixelmem2_23_pixelout), .Store(demultiplexer_2_out22), .Draw(comparator_1_eq));
  pixelmem2 pixelmem2_24 (
    .Data(rom_2_data), .PixelOut(pixelmem2_24_pixelout), .Store(demultiplexer_2_out23), .Draw(comparator_1_eq));
  pixelmem2 pixelmem2_25 (
    .Data(rom_2_data), .PixelOut(pixelmem2_25_pixelout), .Store(demultiplexer_2_out24), .Draw(comparator_1_eq));
  pixelmem2 pixelmem2_26 (
    .Data(rom_2_data), .PixelOut(pixelmem2_26_pixelout), .Store(demultiplexer_2_out25), .Draw(comparator_1_eq));
  pixelmem2 pixelmem2_27 (
    .Data(rom_2_data), .PixelOut(pixelmem2_27_pixelout), .Store(demultiplexer_2_out26), .Draw(comparator_1_eq));
  pixelmem2 pixelmem2_28 (
    .Data(rom_2_data), .PixelOut(pixelmem2_28_pixelout), .Store(demultiplexer_2_out27), .Draw(comparator_1_eq));
  pixelmem2 pixelmem2_29 (
    .Data(rom_2_data), .PixelOut(pixelmem2_29_pixelout), .Store(demultiplexer_2_out28), .Draw(comparator_1_eq));
  pixelmem2 pixelmem2_30 (
    .Data(rom_2_data), .PixelOut(pixelmem2_30_pixelout), .Store(demultiplexer_2_out29), .Draw(comparator_1_eq));
  pixelmem2 pixelmem2_31 (
    .Data(rom_2_data), .PixelOut(pixelmem2_31_pixelout), .Store(demultiplexer_2_out30), .Draw(comparator_1_eq));
  pixelmem2 pixelmem2_32 (
    .Data(rom_2_data), .PixelOut(pixelmem2_32_pixelout), .Store(demultiplexer_2_out31), .Draw(comparator_1_eq));
  not not_1 (not_1_out, clock_1_out);
  Counter #(.width(20), .max('hfffff)) Address (.Q(Address_q), .clk(clock_1_out));  // open: load, D, count, carry, clr
  DotMatrix #(.inputtype("row"), .matrixcols(32), .matrixrows(32), .persist(1)) dotmatrix_3 (
    .row0(pixelmem2_33_pixelout), .row1(pixelmem2_34_pixelout), .row2(pixelmem2_35_pixelout),
    .row3(pixelmem2_36_pixelout), .row4(pixelmem2_37_pixelout), .row5(pixelmem2_38_pixelout),
    .row6(pixelmem2_39_pixelout), .row7(pixelmem2_40_pixelout), .row8(pixelmem2_41_pixelout),
    .row9(pixelmem2_42_pixelout), .row10(pixelmem2_43_pixelout), .row11(pixelmem2_44_pixelout),
    .row12(pixelmem2_45_pixelout), .row13(pixelmem2_46_pixelout), .row14(pixelmem2_47_pixelout),
    .row15(pixelmem2_48_pixelout), .row16(pixelmem2_49_pixelout), .row17(pixelmem2_50_pixelout),
    .row18(pixelmem2_51_pixelout), .row19(pixelmem2_52_pixelout), .row20(pixelmem2_53_pixelout),
    .row21(pixelmem2_54_pixelout), .row22(pixelmem2_55_pixelout), .row23(pixelmem2_56_pixelout),
    .row24(pixelmem2_57_pixelout), .row25(pixelmem2_58_pixelout), .row26(pixelmem2_59_pixelout),
    .row27(pixelmem2_60_pixelout), .row28(pixelmem2_61_pixelout), .row29(pixelmem2_62_pixelout),
    .row30(pixelmem2_63_pixelout), .row31(pixelmem2_64_pixelout));
  DotMatrix #(.inputtype("row"), .matrixcols(32), .matrixrows(32), .persist(1)) dotmatrix_4 (
    .row0(pixelmem_33_pixelout), .row1(pixelmem_34_pixelout), .row2(pixelmem_35_pixelout),
    .row3(pixelmem_36_pixelout), .row4(pixelmem_37_pixelout), .row5(pixelmem_38_pixelout),
    .row6(pixelmem_39_pixelout), .row7(pixelmem_40_pixelout), .row8(pixelmem_41_pixelout),
    .row9(pixelmem_42_pixelout), .row10(pixelmem_43_pixelout), .row11(pixelmem_44_pixelout),
    .row12(pixelmem_45_pixelout), .row13(pixelmem_46_pixelout), .row14(pixelmem_47_pixelout),
    .row15(pixelmem_48_pixelout), .row16(pixelmem_49_pixelout), .row17(pixelmem_50_pixelout),
    .row18(pixelmem_51_pixelout), .row19(pixelmem_52_pixelout), .row20(pixelmem_53_pixelout),
    .row21(pixelmem_54_pixelout), .row22(pixelmem_55_pixelout), .row23(pixelmem_56_pixelout),
    .row24(pixelmem_57_pixelout), .row25(pixelmem_58_pixelout), .row26(pixelmem_59_pixelout),
    .row27(pixelmem_60_pixelout), .row28(pixelmem_61_pixelout), .row29(pixelmem_62_pixelout),
    .row30(pixelmem_63_pixelout), .row31(pixelmem_64_pixelout));
  Counter #(.width(5), .max('h1f)) Row (.Q(Row_q), .clk(clock_1_out));  // open: load, D, count, carry, clr
  Comparator #(.width(5), .mode("unsigned")) comparator_1 (
    .a(Row_q), .b({5{1'b0}}), .eq(comparator_1_eq));  // open: gt, lt
  Counter #(.width(32), .max('hffffffff)) counter_1 (
    .Q(counter_1_q), .clk(comparator_1_eq));  // open: load, D, count, carry, clr
  // Probe on counter_1_q
  pixelmem2 pixelmem2_33 (
    .Data(rom_3_data), .PixelOut(pixelmem2_33_pixelout), .Store(demultiplexer_3_out0), .Draw(comparator_1_eq));
  pixelmem2 pixelmem2_34 (
    .Data(rom_3_data), .PixelOut(pixelmem2_34_pixelout), .Store(demultiplexer_3_out1), .Draw(comparator_1_eq));
  pixelmem2 pixelmem2_35 (
    .Data(rom_3_data), .PixelOut(pixelmem2_35_pixelout), .Store(demultiplexer_3_out2), .Draw(comparator_1_eq));
  pixelmem2 pixelmem2_36 (
    .Data(rom_3_data), .PixelOut(pixelmem2_36_pixelout), .Store(demultiplexer_3_out3), .Draw(comparator_1_eq));
  pixelmem2 pixelmem2_37 (
    .Data(rom_3_data), .PixelOut(pixelmem2_37_pixelout), .Store(demultiplexer_3_out4), .Draw(comparator_1_eq));
  pixelmem2 pixelmem2_38 (
    .Data(rom_3_data), .PixelOut(pixelmem2_38_pixelout), .Store(demultiplexer_3_out5), .Draw(comparator_1_eq));
  pixelmem2 pixelmem2_39 (
    .Data(rom_3_data), .PixelOut(pixelmem2_39_pixelout), .Store(demultiplexer_3_out6), .Draw(comparator_1_eq));
  pixelmem2 pixelmem2_40 (
    .Data(rom_3_data), .PixelOut(pixelmem2_40_pixelout), .Store(demultiplexer_3_out7), .Draw(comparator_1_eq));
  pixelmem2 pixelmem2_41 (
    .Data(rom_3_data), .PixelOut(pixelmem2_41_pixelout), .Store(demultiplexer_3_out8), .Draw(comparator_1_eq));
  pixelmem2 pixelmem2_42 (
    .Data(rom_3_data), .PixelOut(pixelmem2_42_pixelout), .Store(demultiplexer_3_out9), .Draw(comparator_1_eq));
  pixelmem2 pixelmem2_43 (
    .Data(rom_3_data), .PixelOut(pixelmem2_43_pixelout), .Store(demultiplexer_3_out10), .Draw(comparator_1_eq));
  pixelmem2 pixelmem2_44 (
    .Data(rom_3_data), .PixelOut(pixelmem2_44_pixelout), .Store(demultiplexer_3_out11), .Draw(comparator_1_eq));
  pixelmem2 pixelmem2_45 (
    .Data(rom_3_data), .PixelOut(pixelmem2_45_pixelout), .Store(demultiplexer_3_out12), .Draw(comparator_1_eq));
  pixelmem2 pixelmem2_46 (
    .Data(rom_3_data), .PixelOut(pixelmem2_46_pixelout), .Store(demultiplexer_3_out13), .Draw(comparator_1_eq));
  pixelmem2 pixelmem2_47 (
    .Data(rom_3_data), .PixelOut(pixelmem2_47_pixelout), .Store(demultiplexer_3_out14), .Draw(comparator_1_eq));
  pixelmem2 pixelmem2_48 (
    .Data(rom_3_data), .PixelOut(pixelmem2_48_pixelout), .Store(demultiplexer_3_out15), .Draw(comparator_1_eq));
  pixelmem2 pixelmem2_49 (
    .Data(rom_3_data), .PixelOut(pixelmem2_49_pixelout), .Store(demultiplexer_3_out16), .Draw(comparator_1_eq));
  pixelmem2 pixelmem2_50 (
    .Data(rom_3_data), .PixelOut(pixelmem2_50_pixelout), .Store(demultiplexer_3_out17), .Draw(comparator_1_eq));
  pixelmem2 pixelmem2_51 (
    .Data(rom_3_data), .PixelOut(pixelmem2_51_pixelout), .Store(demultiplexer_3_out18), .Draw(comparator_1_eq));
  pixelmem2 pixelmem2_52 (
    .Data(rom_3_data), .PixelOut(pixelmem2_52_pixelout), .Store(demultiplexer_3_out19), .Draw(comparator_1_eq));
  pixelmem2 pixelmem2_53 (
    .Data(rom_3_data), .PixelOut(pixelmem2_53_pixelout), .Store(demultiplexer_3_out20), .Draw(comparator_1_eq));
  pixelmem2 pixelmem2_54 (
    .Data(rom_3_data), .PixelOut(pixelmem2_54_pixelout), .Store(demultiplexer_3_out21), .Draw(comparator_1_eq));
  pixelmem2 pixelmem2_55 (
    .Data(rom_3_data), .PixelOut(pixelmem2_55_pixelout), .Store(demultiplexer_3_out22), .Draw(comparator_1_eq));
  pixelmem2 pixelmem2_56 (
    .Data(rom_3_data), .PixelOut(pixelmem2_56_pixelout), .Store(demultiplexer_3_out23), .Draw(comparator_1_eq));
  pixelmem2 pixelmem2_57 (
    .Data(rom_3_data), .PixelOut(pixelmem2_57_pixelout), .Store(demultiplexer_3_out24), .Draw(comparator_1_eq));
  pixelmem2 pixelmem2_58 (
    .Data(rom_3_data), .PixelOut(pixelmem2_58_pixelout), .Store(demultiplexer_3_out25), .Draw(comparator_1_eq));
  pixelmem2 pixelmem2_59 (
    .Data(rom_3_data), .PixelOut(pixelmem2_59_pixelout), .Store(demultiplexer_3_out26), .Draw(comparator_1_eq));
  pixelmem2 pixelmem2_60 (
    .Data(rom_3_data), .PixelOut(pixelmem2_60_pixelout), .Store(demultiplexer_3_out27), .Draw(comparator_1_eq));
  pixelmem2 pixelmem2_61 (
    .Data(rom_3_data), .PixelOut(pixelmem2_61_pixelout), .Store(demultiplexer_3_out28), .Draw(comparator_1_eq));
  pixelmem2 pixelmem2_62 (
    .Data(rom_3_data), .PixelOut(pixelmem2_62_pixelout), .Store(demultiplexer_3_out29), .Draw(comparator_1_eq));
  pixelmem2 pixelmem2_63 (
    .Data(rom_3_data), .PixelOut(pixelmem2_63_pixelout), .Store(demultiplexer_3_out30), .Draw(comparator_1_eq));
  pixelmem2 pixelmem2_64 (
    .Data(rom_3_data), .PixelOut(pixelmem2_64_pixelout), .Store(demultiplexer_3_out31), .Draw(comparator_1_eq));
  pixelmem pixelmem_33 (
    .Data(rom_4_data), .Store(demultiplexer_4_out0), .PixelOut(pixelmem_33_pixelout), .Draw(comparator_1_eq));
  pixelmem pixelmem_34 (
    .Data(rom_4_data), .Store(demultiplexer_4_out1), .PixelOut(pixelmem_34_pixelout), .Draw(comparator_1_eq));
  pixelmem pixelmem_35 (
    .Data(rom_4_data), .Store(demultiplexer_4_out2), .PixelOut(pixelmem_35_pixelout), .Draw(comparator_1_eq));
  pixelmem pixelmem_36 (
    .Data(rom_4_data), .Store(demultiplexer_4_out3), .PixelOut(pixelmem_36_pixelout), .Draw(comparator_1_eq));
  pixelmem pixelmem_37 (
    .Data(rom_4_data), .Store(demultiplexer_4_out4), .PixelOut(pixelmem_37_pixelout), .Draw(comparator_1_eq));
  pixelmem pixelmem_38 (
    .Data(rom_4_data), .Store(demultiplexer_4_out5), .PixelOut(pixelmem_38_pixelout), .Draw(comparator_1_eq));
  pixelmem pixelmem_39 (
    .Data(rom_4_data), .Store(demultiplexer_4_out6), .PixelOut(pixelmem_39_pixelout), .Draw(comparator_1_eq));
  pixelmem pixelmem_40 (
    .Data(rom_4_data), .Store(demultiplexer_4_out7), .PixelOut(pixelmem_40_pixelout), .Draw(comparator_1_eq));
  pixelmem pixelmem_41 (
    .Data(rom_4_data), .Store(demultiplexer_4_out8), .PixelOut(pixelmem_41_pixelout), .Draw(comparator_1_eq));
  pixelmem pixelmem_42 (
    .Data(rom_4_data), .Store(demultiplexer_4_out9), .PixelOut(pixelmem_42_pixelout), .Draw(comparator_1_eq));
  pixelmem pixelmem_43 (
    .Data(rom_4_data), .Store(demultiplexer_4_out10), .PixelOut(pixelmem_43_pixelout), .Draw(comparator_1_eq));
  pixelmem pixelmem_44 (
    .Data(rom_4_data), .Store(demultiplexer_4_out11), .PixelOut(pixelmem_44_pixelout), .Draw(comparator_1_eq));
  pixelmem pixelmem_45 (
    .Data(rom_4_data), .Store(demultiplexer_4_out12), .PixelOut(pixelmem_45_pixelout), .Draw(comparator_1_eq));
  pixelmem pixelmem_46 (
    .Data(rom_4_data), .Store(demultiplexer_4_out13), .PixelOut(pixelmem_46_pixelout), .Draw(comparator_1_eq));
  pixelmem pixelmem_47 (
    .Data(rom_4_data), .Store(demultiplexer_4_out14), .PixelOut(pixelmem_47_pixelout), .Draw(comparator_1_eq));
  pixelmem pixelmem_48 (
    .Data(rom_4_data), .Store(demultiplexer_4_out15), .PixelOut(pixelmem_48_pixelout), .Draw(comparator_1_eq));
  pixelmem pixelmem_49 (
    .Data(rom_4_data), .Store(demultiplexer_4_out16), .PixelOut(pixelmem_49_pixelout), .Draw(comparator_1_eq));
  pixelmem pixelmem_50 (
    .Data(rom_4_data), .Store(demultiplexer_4_out17), .PixelOut(pixelmem_50_pixelout), .Draw(comparator_1_eq));
  pixelmem pixelmem_51 (
    .Data(rom_4_data), .Store(demultiplexer_4_out18), .PixelOut(pixelmem_51_pixelout), .Draw(comparator_1_eq));
  pixelmem pixelmem_52 (
    .Data(rom_4_data), .Store(demultiplexer_4_out19), .PixelOut(pixelmem_52_pixelout), .Draw(comparator_1_eq));
  pixelmem pixelmem_53 (
    .Data(rom_4_data), .Store(demultiplexer_4_out20), .PixelOut(pixelmem_53_pixelout), .Draw(comparator_1_eq));
  pixelmem pixelmem_54 (
    .Data(rom_4_data), .Store(demultiplexer_4_out21), .PixelOut(pixelmem_54_pixelout), .Draw(comparator_1_eq));
  pixelmem pixelmem_55 (
    .Data(rom_4_data), .Store(demultiplexer_4_out22), .PixelOut(pixelmem_55_pixelout), .Draw(comparator_1_eq));
  pixelmem pixelmem_56 (
    .Data(rom_4_data), .Store(demultiplexer_4_out23), .PixelOut(pixelmem_56_pixelout), .Draw(comparator_1_eq));
  pixelmem pixelmem_57 (
    .Data(rom_4_data), .Store(demultiplexer_4_out24), .PixelOut(pixelmem_57_pixelout), .Draw(comparator_1_eq));
  pixelmem pixelmem_58 (
    .Data(rom_4_data), .Store(demultiplexer_4_out25), .PixelOut(pixelmem_58_pixelout), .Draw(comparator_1_eq));
  pixelmem pixelmem_59 (
    .Data(rom_4_data), .Store(demultiplexer_4_out26), .PixelOut(pixelmem_59_pixelout), .Draw(comparator_1_eq));
  pixelmem pixelmem_60 (
    .Data(rom_4_data), .Store(demultiplexer_4_out27), .PixelOut(pixelmem_60_pixelout), .Draw(comparator_1_eq));
  pixelmem pixelmem_61 (
    .Data(rom_4_data), .Store(demultiplexer_4_out28), .PixelOut(pixelmem_61_pixelout), .Draw(comparator_1_eq));
  pixelmem pixelmem_62 (
    .Data(rom_4_data), .Store(demultiplexer_4_out29), .PixelOut(pixelmem_62_pixelout), .Draw(comparator_1_eq));
  pixelmem pixelmem_63 (
    .Data(rom_4_data), .Store(demultiplexer_4_out30), .PixelOut(pixelmem_63_pixelout), .Draw(comparator_1_eq));
  pixelmem pixelmem_64 (
    .Data(rom_4_data), .Store(demultiplexer_4_out31), .PixelOut(pixelmem_64_pixelout), .Draw(comparator_1_eq));
  Demultiplexer #(.select(5)) demultiplexer_3 (
    .out0(demultiplexer_3_out0), .out1(demultiplexer_3_out1), .out2(demultiplexer_3_out2),
    .out3(demultiplexer_3_out3), .out4(demultiplexer_3_out4), .out5(demultiplexer_3_out5),
    .out6(demultiplexer_3_out6), .out7(demultiplexer_3_out7), .out8(demultiplexer_3_out8),
    .out9(demultiplexer_3_out9), .out10(demultiplexer_3_out10), .out11(demultiplexer_3_out11),
    .out12(demultiplexer_3_out12), .out13(demultiplexer_3_out13), .out14(demultiplexer_3_out14),
    .out15(demultiplexer_3_out15), .out16(demultiplexer_3_out16), .out17(demultiplexer_3_out17),
    .out18(demultiplexer_3_out18), .out19(demultiplexer_3_out19), .out20(demultiplexer_3_out20),
    .out21(demultiplexer_3_out21), .out22(demultiplexer_3_out22), .out23(demultiplexer_3_out23),
    .out24(demultiplexer_3_out24), .out25(demultiplexer_3_out25), .out26(demultiplexer_3_out26),
    .out27(demultiplexer_3_out27), .out28(demultiplexer_3_out28), .out29(demultiplexer_3_out29),
    .out30(demultiplexer_3_out30), .out31(demultiplexer_3_out31), .in(not_1_out), .sel(Row_q));  // open: en
  Demultiplexer #(.select(5)) demultiplexer_4 (
    .out0(demultiplexer_4_out0), .out1(demultiplexer_4_out1), .out2(demultiplexer_4_out2),
    .out3(demultiplexer_4_out3), .out4(demultiplexer_4_out4), .out5(demultiplexer_4_out5),
    .out6(demultiplexer_4_out6), .out7(demultiplexer_4_out7), .out8(demultiplexer_4_out8),
    .out9(demultiplexer_4_out9), .out10(demultiplexer_4_out10), .out11(demultiplexer_4_out11),
    .out12(demultiplexer_4_out12), .out13(demultiplexer_4_out13), .out14(demultiplexer_4_out14),
    .out15(demultiplexer_4_out15), .out16(demultiplexer_4_out16), .out17(demultiplexer_4_out17),
    .out18(demultiplexer_4_out18), .out19(demultiplexer_4_out19), .out20(demultiplexer_4_out20),
    .out21(demultiplexer_4_out21), .out22(demultiplexer_4_out22), .out23(demultiplexer_4_out23),
    .out24(demultiplexer_4_out24), .out25(demultiplexer_4_out25), .out26(demultiplexer_4_out26),
    .out27(demultiplexer_4_out27), .out28(demultiplexer_4_out28), .out29(demultiplexer_4_out29),
    .out30(demultiplexer_4_out30), .out31(demultiplexer_4_out31), .in(not_1_out), .sel(Row_q));  // open: en
  ROM #(.addrWidth(20), .dataWidth(32)) rom_3 (.addr(Address_q), .data(rom_3_data));  // open: sel
  ROM #(.addrWidth(20), .dataWidth(32)) rom_4 (.addr(Address_q), .data(rom_4_data));  // open: sel

  // Notes on the sheet:
  //   contents of rom_1 (hex, n*v repeats v):
  //   1877*0 80000000 c0000000 c0000000 5*80000000 21*0 18000000 18000000 30000000 38000000 30000000
  //   70000000 60000000 e0000000 e0000000 e0000000 c0000000 c0000000 c0000000 80000000 e0000000 5*80000000
  //   10*0 1000000 1000000 2000000 2000000 0 0 0 c000000 8000000 18000000 18000000 18000000 30000000
  //   30000000 30000000 20000000 fc000000 fc000000 fc000000 f8000000 9*f0000000 e0000000 e0000000 e0000000
  //   e0001000 e0001000 e0000000 e0002000 c0002000 c0000000 7*e0000000 c0000000 c0000000 c0000000
  //   7*ff000000 8*fe000000 fc000000 fc000200 fc000600 fc000400 fc000c00 fc000c00 fc000800 fc001800
  //   fc001000 8*fc000000 ff800000 ff800000 ffc00000 ffc00000 4*ffe00000 ffc00000 ff800000 ff810000
  //   ffc00000 6*ff800000 ff800080 ff800080 ff800180 ff800100 ff800300 ff800300 ff000600 7*ff800000
  //   ffc00000 ffc00000 ffe00000 ffe00000 fff00000 fff00000 5*fff80000 fff00000 ffe00000 fff00000 fff00000
  //   fff00000 5*ffe00000 ffe00020 ffe00060 ffe00060 ffe00060 ffe000c0 7*ffe00000 4*fff00000 fff80000
  //   fff80000 7*fffc0000 11*fff80000 fff80010 fff80000 fff00000 8*fff80000 fffc0000 fffc0000 fffe0000
  //   fffe0000 6*ffff0000 fffe0000 fffe0000 fffe0800 fffe0800 fffe0800 7*fffe0000 fffc0000 fffc0000
  //   4*fffe0000 fffc0000 fffc0000 fffc0000 fffe0000 fffe0000 fffe0000 ffff0000 6*ffff8000 ffff0000
  //   ffff0000 ffff0000 5*ffff0400 7*ffff0000 4*ffff8000 fffe0000 fffe0000 ffff0000 ffff0000 ffff0000
  //   ffff8000 6*ffffc000 4*ffff8000 8*ffff8200 ffff8000 ffff8000 ffffc000 ffffc800 ffffc800 ffffc000
  //   ffffc000 ffffc000 ffff0000 ffff8000 ffff8000 ffff8000 ffffc000 7*ffffe000 ffffc000 ffffc000 ffffc000
  //   ffffc100 ffffc100 ffffc100 ffffc180 ffffc100 4*ffffc300 ffffc200 ffffc000 ffffe600 ffffe600 ffffe400
  //   ffffe400 ffffe000 ffffe000 ffffc000 ffffc000 ffffc000 ffffe000 ffffe000 6*fffff000 4*ffffe000
  //   ffffe080 ffffe080 ffffe1c0 ffffe1c0 5*ffffe180 ffffe100 fffff300 fffff300 fffff200 fffff200 fffff000
  //   fffff000 fffff000 ffffe000 ffffe000 fffff000 fffff000 6*fffff800 4*fffff000 9*fffff0c0 fffff080
  //   fffff980 fffff980 fffff980 fffff900 4*fffff800 fffff000 fffff800 fffff800 7*fffffc00 fffff800
  //   fffff800 fffff800 5*fffff840 4*fffff860 fffff040 fffff8c0 fffffcc0 fffffcc0 fffffc80 7*fffffc00
  //   8*fffffe00 7*fffffc00 4*fffffc20 fffff820 fffffc20 fffffc60 fffffc60 fffffc40 fffffec0 4*fffffe00
  //   fffffc00 fffffe00 fffffe00 8*ffffff00 10*fffffe00 fffffc00 fffffc00 fffffe20 fffffe20 fffffe60
  //   fffffe60 fffffe00 ffffff00 ffffff00 ffffff00 fffffe00 fffffe00 ffffff00 ffffff00 8*ffffff80
  //   10*ffffff00 fffffe00 fffffe10 ffffff10 ffffff30 ffffff30 ffffff20 ffffff00 ffffff80 ffffff80
  //   ffffff80 ffffff00 ffffff00 ffffff80 ffffff80 ffffff80 ffffffc0 ffffffc0 ffffff80 ffffff80 4*ffffffc0
  //   9*ffffff80 ffffff00 ffffff00 ffffff00 ffffff80 ffffff90 ffffff90 6*ffffff80 fffffe00 ffffff80
  //   ffffff80 7*ffffffc0 4*ffffffe0 8*ffffffc0 ffffff80 ffffff80 ffffff80 7*ffffffc0 fffffc00 fffffe00
  //   9*ffffffc0 ffffffe0 fffffff0 fffffff0 fffffff0 8*ffffffe0 ffffffc0 ffffffc0 ffffffc0 6*ffffffe0
  //   fffffc00 fffffc00 ffffff80 ffffff80 ffffff80 7*ffffffc0 ffffffe0 fffffff0 fffffff0 fffffff0 ffffffe0
  //   fffffff0 fffffff0 fffffff0 6*ffffffe0 fffffff0 fffffff0 fffffff0 ffffffe0 ffffffc0 ffffffc0 fffff800
  //   fffffc00 4*ffffff80 ffffffc0 ffffffc0 ffffff80 ffffff80 ffffff80 ffffffc0 ffffffe0 ffffffe0
  //   14*fffffff0 ffffffe0 ffffffc0 ffffff80 ffffff80 fffff800 ffffff00 ffffff00 ffffff00 4*ffffff80
  //   ffffff00 ffffff00 ffffff80 ffffffc0 ffffffc0 ffffffe0 ffffffe0 ffffffe0 7*fffffff0 ffffffe0 fffffff0
  //   fffffff0 ffffffe0 ffffffc0 ffffff80 ffffff00 ffffff00 fffffe00 6*ffffff00 4*fffffe00 ffffff80
  //   ffffff80 ffffffc0 ffffffc0 ffffffc0 ffffffe0 ffffffe0 5*fffffff0 ffffffc0 ffffffe0 ffffffe0 ffffffc0
  //   ffffff80 ffffff00 fffffe00 fffffe00 fffffc00 fffffc00 5*fffffe00 4*fffffc00 ffffff00 4*ffffff80
  //   ffffffc0 ffffffc0 ffffffe0 ffffffe0 fffffff0 fffffff0 fffffff0 ffffff80 ffffffc0 ffffffc0 ffffff80
  //   ffffff00 fffffe00 fffffe00 fffffc00 fffffc00 fffff800 fffff800 fffffe00 fffffe00 fffffc00 fffffc00
  //   fffffc00 fffff800 fffff800 fffff800 fffffe00 ffffff00 ffffff00 ffffff00 ffffff80 ffffff80 ffffff80
  //   ffffffc0 ffffffc0 4*ffffffe0 fff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
  //   contents of rom_2 (hex, n*v repeats v):
  //   1888*0 80000000 31*0 60000000 40000000 40000000 80000000 28*0 8*c0000000 4*80000000 20*0 fc000000
  //   fc000000 4*f8000000 f0000000 f0000000 e0000000 e0000000 e0000000 c0000000 c0000000 4*80000000 15*0
  //   ff800000 ff000000 ff000000 ff000000 fe000000 fe000000 fc000000 fc000000 fc000000 f8000000 f8000000
  //   f0000000 f0000000 4*e0000000 c0000000 4*80000000 10*0 ffe00000 ffe00000 ffe00000 ffc00000 ffc00000
  //   ff800000 ff800000 ff000000 ff000000 fe000000 fe000000 fc000000 fc000000 4*f8000000 f0000000 e0000000
  //   e0000000 e0000000 c0000000 c0000000 c0000000 4*80000000 4*0 4*fff80000 fff00000 fff00000 ffe00000
  //   ffe00000 ffc00000 ffc00000 ff800000 ff800000 ff000000 ff000000 fe000000 fe000000 fe000000 fc000000
  //   f8000000 f8000000 f8000000 f0000000 f0000000 f0000000 4*e0000000 c0000000 c0000000 c0000000 80000000
  //   4*fffe0000 fffc0000 fffc0000 fff80000 fff80000 fff00000 fff00000 ffe00000 ffe00000 ffc00000 ffc00000
  //   ff800000 ff800000 ff800000 ff000000 fe000000 fe000000 fe000000 fc000000 fc000000 4*f8000000 f0000000
  //   f0000000 f0000000 e0000000 e0000000 ffff8000 ffff8000 ffff8000 ffff0000 ffff0000 fffe0000 fffe0000
  //   fffc0000 fffc0000 fff80000 fff80000 fff00000 fff00000 ffe00000 ffe00000 ffe00000 ffc00000 ff800000
  //   ff800000 ff800000 ff000000 ff000000 4*fe000000 fc000000 fc000000 fc000000 f8000000 f8000000 f8000000
  //   ffffc000 ffffc000 ffffc000 ffff8000 ffff8000 ffff0000 ffff0000 ffff0000 fffe0000 fffe0000 fffc0000
  //   fffc0000 fff80000 fff80000 fff80000 fff00000 fff00000 ffe00000 ffe00000 ffc00000 ffc00000 ff800000
  //   ff800000 ff800000 ff000000 ff000000 ff000000 4*fe000000 fc000000 ffffe000 ffffe000 ffffc000 ffffc000
  //   ffffc000 4*ffff8000 ffff0000 ffff0000 fffe0000 fffe0000 fffe0000 fffc0000 fff80000 fff80000 fff00000
  //   fff00000 fff00000 ffe00000 ffe00000 ffe00000 ffc00000 ffc00000 ffc00000 4*ff800000 ff000000 ff000000
  //   fffff000 4*ffffe000 5*ffffc000 ffff8000 ffff8000 ffff0000 ffff0000 fffe0000 fffc0000 6*fff80000
  //   fff00000 fff00000 fff00000 ffe00000 ffe00000 ffe00000 4*ffc00000 fffff800 4*fffff000 5*ffffe000
  //   ffffc000 ffffc000 ffff0000 fffe0000 fffe0000 4*fffc0000 fffe0000 fffc0000 fffc0000 fffc0000
  //   4*fff80000 fff00000 fff00000 fff00000 ffe00000 ffe00000 6*fffff800 4*fffff000 ffffc000 ffff8000
  //   ffff0000 ffff0000 ffff0000 fffe0000 5*ffff0000 4*fffe0000 fffc0000 fffc0000 fffc0000 4*fff80000
  //   6*fffffc00 fffff800 fffff800 fffff800 ffffe000 ffffc000 7*ffff8000 ffffc000 ffffc000 ffff8000
  //   ffff8000 4*ffff0000 4*fffe0000 fffc0000 fffc0000 5*fffffe00 fffffc00 fffffc00 fffffc00 fffff000
  //   ffffe000 6*ffffc000 ffffe000 ffffe000 ffffe000 4*ffffc000 4*ffff8000 4*ffff0000 fffe0000 ffffff00
  //   ffffff00 ffffff00 4*fffffe00 fffff800 fffff000 6*ffffe000 5*fffff000 4*ffffe000 ffffc000 ffffc000
  //   ffffc000 4*ffff8000 ffff0000 ffffff80 ffffff80 5*ffffff00 fffffc00 fffff000 fffff000 fffff000
  //   ffffe000 fffff000 fffff000 fffff000 fffff800 fffff800 fffff800 5*fffff000 ffffe000 ffffe000 ffffe000
  //   ffffc000 ffffc000 ffffc000 ffff8000 ffff8000 ffff8000 ffffffc0 6*ffffff80 ffffff00 fffffc00 fffff800
  //   4*fffff000 fffff800 fffff800 fffffc00 4*fffff800 fffff000 fffff000 fffff000 ffffe000 ffffe000
  //   ffffe000 ffffc000 ffffc000 ffffc000 ffff8000 ffff8000 ffffffc0 ffffffc0 6*ffffff80 fffffe00
  //   7*fffff800 fffffc00 fffffc00 fffff800 fffff800 fffff800 fffff000 fffff000 fffff000 ffffe000 ffffe000
  //   ffffe000 ffffc000 ffffc000 ffffc000 ffff8000 ffff8000 5*ffffff80 ffffff00 ffffff00 ffffff00 fffffc00
  //   fffff800 4*fffff000 6*fffff800 fffff000 fffff000 fffff000 ffffe000 ffffe000 ffffe000 ffffc000
  //   ffffc000 ffffc000 ffff8000 ffff8000 ffff8000 7*ffffff00 fffffc00 fffff800 6*fffff000 fffff800
  //   fffff800 fffff800 4*fffff000 ffffe000 ffffe000 ffffe000 ffffc000 ffffc000 ffffc000 ffff8000 ffff8000
  //   ffff8000 ffff0000 7*fffffe00 fffff800 fffff000 4*ffffe000 7*fffff000 ffffe000 ffffe000 ffffe000
  //   ffffc000 ffffc000 ffffc000 ffff8000 ffff8000 ffff8000 ffff0000 ffff0000 ffff0000 6*fffffc00 fffff800
  //   ffffe000 ffffe000 ffffc000 ffffc000 ffffc000 ffffe000 fffff000 fffff000 fffff000 5*ffffe000 ffffc000
  //   ffffc000 ffffc000 ffff8000 ffff8000 ffff8000 ffff0000 ffff0000 ffff0000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
  //   contents of rom_3 (hex, n*v repeats v):
  //   1406*0 22*1 10*3 7 7 5*f 17*7 8*f 1f 1f 0 0 0 20 20 20 30 30 30 4*38 3c 3c 1c 1e 1e 1e 1f 1f 11*3f
  //   19*0 80 80 80 c0 c0 c0 e0 e0 e0 40e0 40e0 e1 7f 25*0 10000 10000 10000 18000 8180 580 580 3f 3f 3f
  //   6*1f 7*f 4*7 3 3 1 1 7 7*1f 1fff 1fff 9*fff 10*7ff 3ff 3ff 3ff 1ff 1ff 1ff 3ff fff 1fff 1fff 1fff
  //   11*3ffff 15*1ffff 6*ffff 1fffff 13*3fffff 10*1fffff 4*fffff 4*1fffff 7fffff 7fffff 20*ffffff 7fffff
  //   7fffff 7fffff bfffff 5*ffffff 7fffff 3fffff 3fffff 3fffff 7fffff 7fffff 7fffff ffffff ffffff
  //   4*1ffffff 9*3ffffff 1ffffff 1ffffff 1ffffff ffffff 7fffff 7fffff ffffff ffffff 1ffffff 1ffffff
  //   3ffffff fffff fffff 1fffff 1fffff 3fffff 3fffff 3fffff 7fffff 7fffff ffffff ffffff 1ffffff 1ffffff
  //   4*3ffffff 5*7ffffff ffffff fffff 1fffff 1fffff 3fffff 3fffff 7fffff 7fffff 3fffff 1fffff 7ffff 7ffff
  //   7ffff fffff 4fffff 1fffff 1fffff 1fffff 3fffff 3fffff 7fffff 7fffff ffffff 1ffffff 1ffffff 4*3ffffff
  //   7ffffff 3fffff 3ffff 7ffff 7ffff 4*fffff 7ffff 3ffff 1ffff ffff 1ffff 3ffff 3ffff 13ffff 7ffff
  //   27ffff 2fffff 2fffff fffff 1fffff 7fffff 7fffff 7fffff ffffff ffffff ffffff 1ffffff 1ffffff 1ffffff
  //   ffff 1ffff 1ffff 5*3ffff ffff 7fff 3fff 1fff fff ffff 1ffff 1ffff 9ffff bffff 3ffff 7ffff 7ffff
  //   7ffff 1fffff 1fffff 1fffff 3fffff 3fffff 3fffff 7fffff 7fffff 7fffff 7fff 7fff 4*ffff 1ffff ffff
  //   7fff 3fff 1fff fff 7ff 3ff 7fff ffff ffff 1ffff 1ffff 1ffff 3ffff 3ffff 7ffff 7ffff 7ffff 4*fffff
  //   1fffff 1fffff 1fffff 3fff 4*7fff ffff ffff 7fff 3fff fff 7ff 3ff 3ff 1ff 7fff 7fff ffff ffff 6*1ffff
  //   4*3ffff 7ffff 7ffff 7ffff fffff 7fff 3fff 4*7fff ffff 7fff 3fff fff 7ff 3ff 3ff 1ff 7*7fff 6*ffff
  //   4*1ffff 3ffff 3ffff 3fff 3fff 5*7fff 3fff 1fff fff 7ff 3ff 1ff 9*3fff 6*7fff 5*ffff 3fff 3fff 3fff
  //   4*7fff 3fff 1fff 7ff 3ff 3ff 11*1fff 7*3fff 4*7fff 3fff 3fff 3fff 7fff 7fff 7fff 3fff fff 7ff 3ff ff
  //   19*1fff bfff bfff bfff 3fff 1fff 3fff 3fff 3fff 7fff 3fff 1fff fff 7f 7f ff 17*fff 4fff 4*5fff
  //   4*1fff 3fff 3fff 1fff ff ff ff 1ff 15*fff 4*2fff 27ff 37ff 1fff 1fff 4*3fff fff ff ff ff 1ff 6*fff
  //   8*7ff 17ff 17ff 17ff 9*1fff fff 7ff ff ff 1ff 5*fff 8*7ff 3ff bff bff bff fff fff fff 7*7ff 3ff 1ff
  //   ff 1ff 1ff 5*fff 6*7ff 3ff 3ff bff 7*7ff 3ff 3ff 7ff 7ff 7ff 3ff 1ff 1ff ff 1ff 7ff 5*fff 6*7ff 3ff
  //   3ff 4*7ff 3ff 3ff 4*7ff 17ff 3ff 3ff 1ff ff ff ff 1ff 7ff 7ff 7ff 4*fff 15*7ff 13ff 1bff 7ff 3ff 1ff
  //   ff 7f 7f ff 3ff 4*7ff 6*fff 7ff 7ff 7ff 5*fff 7ff 7ff 7ff fff 1fff fff 3ff 1ff ff 7f 7f 3f ff 3ff
  //   3ff 3ff 4*7ff 12*fff 7ff 7ff 7ff fff fff 3ff 1ff ff 7f 3f 3f 3f ff 4*3ff 4*7ff 7*fff 1fff 1fff fff
  //   fff 7ff 7ff 7ff fff 7ff 3ff ff 7f 7f 3f 3f 3f ff 1ff 5*3ff 7ff 7ff 7ff 5*fff 5*1fff 5*7ff 3ff ff 7f
  //   3f 3f 3f 1f 7f 7f ff 1ff 5*3ff 7ff 7ff 7ff 4*fff 5*1fff 5*7ff 3ff ff 7f 7f 3f 3f ff ff 7f ff ff 1ff
  //   4*3ff 4*7ff fff fff fff 5*1fff fff fff 4*7ff 3ff 1ff ff 7f ff ff 1ff 1ff ff 1ff 1ff 3ff 5*7ff 17*fff
  //   3ff 1ff 8*3ff 7ff 5*fff 1fff 1fff 8*fff 6*1fff 7ff 3ff 6*7ff fff fff fff 11*1fff 4*fff 6*1fff fff
  //   7ff 1fff 1fff fff 5*1fff 6*3fff 9*1fff 6*3fff 1fff 1fff fff 6*3fff 7fff 7fff 7fff ffff 7fff 7fff
  //   8*3fff 1fff 1fff 3fff 3fff 3fff 4*7fff 3fff 1fff 1fff 6*7fff ffff ffff 1ffff 1ffff 1ffff ffff 7*7fff
  //   3fff 3fff 6*7fff ffff 7fff 7fff 3fff 3fff 7fff 5*ffff 1ffff 1ffff 3ffff 3ffff 3ffff 1ffff 1ffff
  //   7*ffff 7fff 5*ffff 1ffff 1ffff ffff ffff 7fff 7fff ffff ffff 5*1ffff 3ffff 4*7ffff 3ffff 3ffff
  //   13*1ffff 3ffff 1ffff 1ffff 4*ffff 1ffff 5*3ffff 7ffff 7ffff fffff fffff 4*7ffff 13*3ffff 1ffff 1ffff
  //   1ffff ffff ffff 1ffff 1ffff 4*3ffff 7ffff 8*fffff 12*7ffff 3ffff 3ffff 1ffff ffff 1ffff 1ffff 1ffff
  //   3ffff 5*7ffff fffff 6*1fffff 12*fffff 7ffff 7ffff 3ffff 1ffff 1ffff 1ffff 3ffff 3ffff 7ffff 7ffff
  //   4*fffff 1fffff 5*3fffff 12*1fffff fffff fffff 7ffff 1ffff 1ffff 3ffff 3ffff 3ffff 7ffff 7ffff fffff
  //   fffff fffff 1fffff 1fffff 1fffff 3fffff 7fffff 7fffff 7fffff 12*3fffff 1fffff 1fffff fffff 1ffff
  //   3ffff 3ffff 3ffff 7ffff 7ffff fffff fffff 4*1fffff 3fffff 3fffff 15*7fffff 3fffff 3fffff 1fffff
  //   3ffff 3ffff 3ffff 7ffff 7ffff fffff fffff 1fffff 1fffff 4*3fffff 7fffff 7fffff 9*ffffff 7fffff
  //   7fffff ffffff ffffff 7fffff 7fffff 3fffff 3fffff 3ffff 3ffff 7f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
  //   contents of rom_4 (hex, n*v repeats v):
  //   1376*0 1 31*0 7 7 7 10*f 7 3 17*0 9*1f 7f 7f 3f 1f f 3 1 16*0 5*3f bf 5*ff 7f 3f 1f f 7 7 3 1 1 12*0
  //   7f 17f 17f 17f 1ff 6*3ff 1ff ff 7f 7f 3f 3f 1f 1f f f 7 7 7 5*3 1 1 1 7c0 7c0 7c0 7e0 7e0 fe0 ff0
  //   1ff0 1ff0 1ff8 ff8 7f8 7fc 3fc 1fc 1fe 1fe ff ff 4*7f 9*3f 1000f 4*f 4*200f 300f 100f 100f 100f 80f
  //   807 11*7 5*1f 3f 17*1fff 4*fff 7ff 7ff 5*3ff 1ff 1ff ff ff ffff 3ffff 7ffff 7ffff 7ffff 7*3ffff
  //   1ffff ffff ffff ffff 7fff 7fff 7fff 3fff 3fff 1fff 1fff 1fff fff fff 4*7ff 3ff 3ff fffff fffff
  //   8*1fffff fffff fffff 7ffff 7ffff 3ffff 3ffff 1ffff 1ffff 1ffff ffff ffff 7fff 7fff 7fff 3fff 3fff
  //   1fff 1fff 1fff fff 7ff 3ff 7fffff 2ffffff 1ffffff ffffff ffffff 7fffff 3fffff 1fffff fffff 7ffff
  //   3ffff 3ffff 1ffff ffff ffff ffff 6*7fff 5*3fff 1fff 7ff 3ff 1ff ff 1ffffff 7fffff 3fffff 1fffff
  //   fffff 3ffff 3ffff 1ffff ffff ffff 7fff 7fff 3fff 3fff 3fff 11*1fff 7ff 3ff 1ff ff 7f 7f 7ffff 3ffff
  //   1ffff ffff 7fff 3fff 3fff 1fff 1fff fff fff fff 13*7ff 3ff ff 7f 3f 3f 1f 1f 7fff 3fff 1fff fff fff
  //   7ff 7ff 3ff 3ff 3ff 14*1ff ff 7f 3f 1f f 7 7 7 7ff 7ff 3ff 1ff 1ff 5*ff 6*7f 7*ff 7f 1f f 7 3 3 1 1
  //   1 1ff 1ff ff ff 7f 7f 7f 11*3f 5*7f 1f 7 3 1 1 4*0 ff ff 7f 7f 18*3f 1f 7 3 1 6*0 ff ff 7f 7f 15*3f
  //   4*1f 3 1 7*0 ff ff 7f 7f 7f 12*3f 6*1f 1 8*0 1ff ff ff 7f 7f 11*3f 6*1f f 9*0 1ff 1ff ff 7f 7f 7f
  //   10*3f 6*1f f 9*0 3ff 1ff 1ff ff ff 7f 7f 9*3f 6*1f f 1 8*0 7ff 3ff 1ff 1ff ff 7f 7f 7f 8*3f 6*1f f
  //   9*0 7ff 3ff 1ff ff ff 4*7f 7*3f 5*1f f 10*0 3ff 1ff ff ff 4*7f 7*3f 5*1f f 11*0 1ff ff ff 4*7f 7*3f
  //   5*1f 13*0 ff 4*7f 8*3f 4*1f f 8*0 1 1 4*0 7f 7f 7f 8*3f 5*1f f 8*0 1 5*0 800 8*3f 6*1f f f 7*0 1 1 0
  //   0 0 4*800 5*3f 7*1f f f f 7*0 1 1 0 7*800 3f 3f 8*1f 4*f 7*0 1 1 0 5*800 1800 1800 1800 9*1f 4*f 6*0
  //   1 1 1 801 800 800 800 6*1800 9*1f f f f 1 5*0 1 1 1 801 801 1801 8*1800 4*3f 8*1f f 1 0 0 0 1 4*3
  //   1003 1003 1003 1001 1001 4*3001 3000 7f 12*3f 1f 3 3 1 1 3 7 7 f f 4*7 5*2007 ff ff 12*7f 1f 4*7 f f
  //   7*1f f f 400f 400f 1ff 1ff 1ff 10*ff 7f 1f f f f 1f 10*3f 1f 1f 1f 11*3ff 1ff ff 3f 3f 1f 3f 3f
  //   11*7f 3f 3f 3f 11*7ff ff 7f 7f 7f ff ff 1ff 201ff 201ff 601ff 5*600ff e00ff c00ff c007f c007f c007f
  //   c003f 5*1fff 5*fff 1ff ff ff 1ff 1ff 3ff 403ff 4*c03ff 6*1c01ff 1c00ff 1c00ff 1c00ff 1c007f 1c007f
  //   7*3fff 101fff 101fff 4*3ff 7ff 7ff 1807ff 1807ff 1807ff 3807ff 3807ff 3807ff 5*3803ff 3801ff 3801ff
  //   3801ff 3800ff 3800ff 3800ff 5*7fff 3fff 203fff 203fff 200fff 7ff 2007ff fff fff 201fff 301fff 301fff
  //   6*700fff 4*f007ff 7003ff 7003ff 7003ff 7001ff 7001ff 7001ff ffff ffff 7fff 7fff 7fff 3fff 3fff 3fff
  //   1fff fff 1fff 1fff 1fff 401fff 601fff 601fff 7*e01fff e00fff e00fff e00fff e007ff e007ff e007ff
  //   e003ff e003ff e003ff 4*ffff 7fff 7fff 7fff 6*3fff 5*c01fff 9*1c01fff 1c00fff 1c00fff 1c00fff 1c007ff
  //   1c007ff 1ffff 1ffff ffff ffff ffff 4*7fff 4*3fff 803fff 803fff 803fff 1803fff 13*1801fff 1800fff
  //   1800fff 3ffff 3ffff 1ffff 1ffff 4*ffff 4*7fff 3fff 3fff 4*1003fff 3003fff 3003fff 3003fff 3001fff
  //   3001fff 3003fff 8*3001fff 7ffff 3ffff 3ffff 3ffff 1ffff 1ffff 4*ffff 6*7fff 3fff 4*2003fff 4*6003fff
  //   7*2003fff fffff 7ffff 7ffff 3ffff 3ffff 3ffff 1ffff 1ffff 1ffff 4*ffff 7fff 7fff 7fff 47fff 47fff
  //   47fff 4047fff 4043fff 9*4003fff 6003fff 6003fff 1fffff fffff fffff 7ffff 7ffff 7ffff 3ffff 3ffff
  //   4*1ffff ffff ffff 8ffff 8ffff 8ffff 87fff 87fff c7fff 4047fff c047fff 4*c007fff 6*4003fff 1fffff
  //   1fffff 1fffff fffff fffff 7ffff 7ffff 7ffff 3ffff 3ffff 3ffff 1ffff 1ffff 11ffff 11ffff 10ffff
  //   10ffff 18ffff 8ffff 8ffff 808ffff 7*8007fff 7fff 7fff 7fff 4003fff 3fffff 3fffff 1fffff 1fffff fffff
  //   fffff fffff 7ffff 7ffff 7ffff 4*3ffff 1ffff 11ffff 11ffff 11ffff 10ffff 7*ffff 6*7fff 7fffff 3fffff
  //   3fffff 3fffff 1fffff 1fffff fffff fffff fffff 4*7ffff 4*3ffff 6*1ffff 7*ffff 7fff 7fff 7fffff 7fffff
  //   7fffff 3fffff 3fffff 1fffff 1fffff 1fffff fffff fffff fffff 4*7ffff 6*3ffff 6*1ffff 4*ffff 2ffff
  //   ffffff ffffff 7fffff 7fffff 3fffff 3fffff 3fffff 1fffff 1fffff 1fffff 4*fffff 5*7ffff 6*3ffff
  //   6*1ffff 7ffff 1ffffff ffffff ffffff 7fffff 7fffff 4*3fffff 4*1fffff 5*fffff 5*7ffff 7*3ffff 7ffff
  //   7ffff 1ffffff 1ffffff ffffff ffffff 4*7fffff 4*3fffff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
endmodule

module pixelmem (
  input  [31:0] Data,
  input  Store,
  input  Draw,
  output [31:0] PixelOut
);

  wire [31:0] register_2_q;

  Register #(.width(32)) register_1 (.D(register_2_q), .Q(PixelOut), .clk(Draw));  // open: en, clr
  Register #(.width(32)) register_2 (.D(Data), .Q(register_2_q), .clk(Store));  // open: en, clr
endmodule

module pixelmem2 (
  input  [31:0] Data,
  input  Store,
  input  Draw,
  output [31:0] PixelOut
);

  wire [31:0] register_2_q;

  Register #(.width(32)) register_1 (.D(register_2_q), .Q(PixelOut), .clk(Draw));  // open: en, clr
  Register #(.width(32)) register_2 (.D(Data), .Q(register_2_q), .clk(Store));  // open: en, clr
endmodule
